// Logisim project Automated_Chess.circ as structural Verilog: 10 circuits, main circuit main
module main (
  input  [2:0] X,
  input  [2:0] Y,
  input  [2:0] S,
  output Start_Stop_prime,
  output [2:0] Dir,
  output New
);

  wire clk_out, reset_out;

  Clock clk (.out(clk_out));
  Button reset (.out(reset_out));
  Chess chess_1 (
    .X(X), .Y(Y), .Select(S), .Clk(clk_out), .Reset(reset_out), .Stop_Start(Start_Stop_prime),
    .Direction(Dir), .New(New));

  // Notes on the sheet:
  //   Inputs
  //   For X & Y
  //   000 - 111
  //   For Select
  //   0XX - Knight
  //   110 - King
  //   111 - Rook
  //   100 - Bishop
  //   101 - Queen
  //   Asynchronous reset to initial values
  //   For Reset
  //   1,0 - Knight
  //   2,0 - Bishop
  //   3,0 - Queen
  //   4,0 - King
  //   0,0 - Rook
  //   (X,Y) coordinates
  //   Automated Chess
  //   For New
  //   0 - In process
  //   1 - Give new input
  //   Outputs
  //   For Start/Stop'
  //   0 - Stop
  //   1 - Start/Go
  //   For Direction
  //   000 - E
  //   001 - NE
  //   010 - N
  //   011 - NW
  //   100 - W
  //   101 - SW
  //   110 - S
  //   111 - SE
  //   title size 64 as 8x8 chess board
  //   Made by:
  //   Aarabdh Tiwari  -- 2019AAPS0241G
  //   Aayush kabra  -- 2019AAPS0222G
  //   Aditya Agarwal  -- 2019AAPS0243G
  //   Ashutosh Gupta  -- 2019AAPS0223G
  //   Sarvesh Garge  -- 2019AAPS0233G
  //   Siddhant Sharma  -- 2019AAPS0226G
endmodule

// CHESS
module Chess (
  input  [2:0] X,
  input  [2:0] Y,
  input  [2:0] Select,
  input  Clk,
  input  Reset,
  output Stop_Start,
  output [2:0] Direction,
  output New
);

  wire path_validation_1_v_bqkr, path_validation_1_v_k, path_validation_1_x_sign, path_validation_1_y_sign;
  wire [2:0] direction_encoding_1_d_bqkr, direction_encoding_1_d_k, input_1_select_2, input_1_x,
       input_1_x_in, input_1_y, input_1_y_in, path_validation_1_dx, path_validation_1_dy;

  \input  input_1 (
    .X_user(X), .Y_user(Y), .Select(Select), .New_in(New), .Moved(Stop_Start), .Reset(Reset),
    .X_in(input_1_x_in), .X(input_1_x), .Y_in(input_1_y_in), .Y(input_1_y), .Select_2(input_1_select_2));
  Path_Validation path_validation_1 (
    .X_in(input_1_x_in), .X(input_1_x), .Y_in(input_1_y_in), .Y(input_1_y), .Select(input_1_select_2),
    .dX(path_validation_1_dx), .X_sign(path_validation_1_x_sign), .V_K(path_validation_1_v_k),
    .dY(path_validation_1_dy), .Y_sign(path_validation_1_y_sign), .V_BQKR(path_validation_1_v_bqkr));
  Direction_Encoding direction_encoding_1 (
    .dX(path_validation_1_dx), .X_sign(path_validation_1_x_sign), .dY(path_validation_1_dy),
    .Y_sign(path_validation_1_y_sign), .Select(input_1_select_2), .V_BQKR(path_validation_1_v_bqkr),
    .V_K(path_validation_1_v_k), .Clk(Clk), .D_BQKR(direction_encoding_1_d_bqkr), .No_Move(New),
    .D_K(direction_encoding_1_d_k));
  Output output_1 (
    .dX(path_validation_1_dx), .dY(path_validation_1_dy), .Select(input_1_select_2),
    .V_K(path_validation_1_v_k), .V_BQKR(path_validation_1_v_bqkr), .D_K(direction_encoding_1_d_k),
    .D_BQKR(direction_encoding_1_d_bqkr), .Clk(Clk), .Start_Stop_prime(Stop_Start), .Dir(Direction));

  // Notes on the sheet:
  //   IC connected
endmodule

// Input
module \input  (
  input  [2:0] X_user,
  input  [2:0] Y_user,
  input  [2:0] Select,
  input  New_in,
  input  Moved,
  input  Reset,
  output [2:0] X_in,
  output [2:0] X,
  output [2:0] Y_in,
  output [2:0] Y,
  output [2:0] Select_2
);

  wire _0XX_out, decoder_1_out0, decoder_1_out1, decoder_1_out2, decoder_1_out3, decoder_1_out4,
       decoder_1_out5, decoder_1_out6, decoder_1_out7;
  wire [2:0] register_edge_1_q, register_edge_2_q, register_edge_3_q, register_edge_4_q, register_edge_5_q,
       register_edge_6_q, register_edge_7_q, register_edge_8_q, register_edge_9_q, register_edge_10_q;

  Register_lvl X_Coordinate (.clk(New_in), .D(X_user), .en(1'b1), .reset(Reset), .val(3'b000), .Q(X_in));
  Register_lvl Y_Coordinate (.clk(New_in), .D(Y_user), .en(1'b1), .reset(Reset), .val(3'b000), .Q(Y_in));
  Register_lvl u_Select (.clk(New_in), .D(Select), .en(1'b1), .reset(Reset), .val(3'b000), .Q(Select_2));
  Decoder #(.select(3)) decoder_1 (
    .out0(decoder_1_out0), .out1(decoder_1_out1), .out2(decoder_1_out2), .out3(decoder_1_out3),
    .out4(decoder_1_out4), .out5(decoder_1_out5), .out6(decoder_1_out6), .out7(decoder_1_out7), .sel(Select_2));  // open: en
  or _0XX (_0XX_out, decoder_1_out0, decoder_1_out1, decoder_1_out2, decoder_1_out3);
  Register_edge register_edge_1 (
    .clk(Moved), .D(X_in), .en(_0XX_out), .reset(Reset), .val(3'b001), .Q(register_edge_1_q));
  Register_edge register_edge_2 (
    .clk(Moved), .D(X_in), .en(decoder_1_out4), .reset(Reset), .val(3'b010), .Q(register_edge_2_q));
  Register_edge register_edge_3 (
    .clk(Moved), .D(X_in), .en(decoder_1_out5), .reset(Reset), .val(3'b011), .Q(register_edge_3_q));
  Register_edge register_edge_4 (
    .clk(Moved), .D(X_in), .en(decoder_1_out6), .reset(Reset), .val(3'b100), .Q(register_edge_4_q));
  Register_edge register_edge_5 (
    .clk(Moved), .D(X_in), .en(decoder_1_out7), .reset(Reset), .val(3'b000), .Q(register_edge_5_q));
  Register_edge register_edge_6 (
    .clk(Moved), .D(Y_in), .en(_0XX_out), .reset(Reset), .val(3'b000), .Q(register_edge_6_q));
  Register_edge register_edge_7 (
    .clk(Moved), .D(Y_in), .en(decoder_1_out4), .reset(Reset), .val(3'b000), .Q(register_edge_7_q));
  Register_edge register_edge_8 (
    .clk(Moved), .D(Y_in), .en(decoder_1_out5), .reset(Reset), .val(3'b000), .Q(register_edge_8_q));
  Register_edge register_edge_9 (
    .clk(Moved), .D(Y_in), .en(decoder_1_out6), .reset(Reset), .val(3'b000), .Q(register_edge_9_q));
  Register_edge register_edge_10 (
    .clk(Moved), .D(Y_in), .en(decoder_1_out7), .reset(Reset), .val(3'b000), .Q(register_edge_10_q));
  Multiplexer #(.select(3), .width(3)) multiplexer_1 (
    .in0(register_edge_1_q), .in1(register_edge_1_q), .in2(register_edge_1_q), .in3(register_edge_1_q),
    .in4(register_edge_2_q), .in5(register_edge_3_q), .in6(register_edge_4_q), .in7(register_edge_5_q),
    .out(X), .sel(Select_2));  // open: en
  Multiplexer #(.select(3), .width(3)) multiplexer_2 (
    .in0(register_edge_6_q), .in1(register_edge_6_q), .in2(register_edge_6_q), .in3(register_edge_6_q),
    .in4(register_edge_7_q), .in5(register_edge_8_q), .in6(register_edge_9_q), .in7(register_edge_10_q),
    .out(Y), .sel(Select_2));  // open: en

  // Notes on the sheet:
  //   Reset value of user registers
  //   0XX - Knight
  //   100 - Bishop
  //   101 - Queen
  //   110 - King
  //   111 - Rook
  //   Ready For New Input
  //   Final Piece Moved
  //   Asynchronous reset to initial values
  //   User Input
  //   White pieces
  //   Reset values of X-coordinate
  //   Knight
  //   Bishop
  //   Queen
  //   King
  //   Rook
  //   Reset value of Y-coordinate
  //   or 6
  //   or 5
  //   or 7
  //   White pieces
  //   Cache
  //   Knight
  //   Bishop
  //   Queen
  //   King
  //   Rook
  //   Y- Coordinate
  //   Knight
  //   Bishop
  //   Queen
  //   King
  //   Rook
  //   X-Coordinate
endmodule

// Valid
module Path_Validation (
  input  [2:0] X_in,
  input  [2:0] X,
  input  [2:0] Y_in,
  input  [2:0] Y,
  input  [2:0] Select,
  output [2:0] dX,
  output X_sign,
  output V_K,
  output [2:0] dY,
  output Y_sign,
  output V_BQKR
);

  wire and_1_out, comparator_1_eq, comparator_2_eq, comparator_3_eq, or_1_out, or_2_out, or_3_out, or_4_out,
       xor_1_out;
  wire [2:0] demultiplexer_1_out0, demultiplexer_1_out1, demultiplexer_2_out0, demultiplexer_2_out1,
       multiplier_1_cout, multiplier_1_out, multiplier_2_cout, multiplier_2_out, negator_1_out,
       negator_2_out, subtractor_1_out, subtractor_2_out;
  wire [5:0] adder_1_out;

  Subtractor #(.width(3)) subtractor_1 (.a(X_in), .b(X), .out(subtractor_1_out), .bout(X_sign));  // open: bin
  Subtractor #(.width(3)) subtractor_2 (.a(Y_in), .b(Y), .out(subtractor_2_out), .bout(Y_sign));  // open: bin
  Negator #(.width(3)) negator_1 (.in(subtractor_1_out), .out(negator_1_out));
  Negator #(.width(3)) negator_2 (.in(subtractor_2_out), .out(negator_2_out));
  Multiplexer #(.width(3)) multiplexer_1 (
    .in0(subtractor_1_out), .in1(negator_1_out), .out(dX), .sel(X_sign));  // open: en
  Demultiplexer #(.width(3)) demultiplexer_1 (
    .out0(demultiplexer_1_out0), .out1(demultiplexer_1_out1), .in(dX), .sel(Select[2]));  // open: en
  Demultiplexer #(.width(3)) demultiplexer_2 (
    .out0(demultiplexer_2_out0), .out1(demultiplexer_2_out1), .in(dY), .sel(Select[2]));  // open: en
  Multiplexer #(.width(3)) multiplexer_2 (
    .in0(subtractor_2_out), .in1(negator_2_out), .out(dY), .sel(Y_sign));  // open: en
  Multiplier #(.width(3)) multiplier_1 (
    .a(demultiplexer_1_out0), .b(demultiplexer_1_out0), .out(multiplier_1_out), .cout(multiplier_1_cout));  // open: cin
  Multiplier #(.width(3)) multiplier_2 (
    .a(demultiplexer_2_out0), .b(demultiplexer_2_out0), .out(multiplier_2_out), .cout(multiplier_2_cout));  // open: cin
  or or_1 (or_1_out, demultiplexer_1_out1[0], demultiplexer_1_out1[1], demultiplexer_1_out1[2]);
  or or_2 (or_2_out, demultiplexer_2_out1[0], demultiplexer_2_out1[1], demultiplexer_2_out1[2]);
  Adder #(.width(6)) adder_1 (
    .a({multiplier_1_cout, multiplier_1_out}), .b({multiplier_2_cout, multiplier_2_out}), .out(adder_1_out));  // open: cin, cout
  Comparator #(.width(3), .mode("unsigned")) comparator_1 (
    .a(demultiplexer_1_out1), .b(3'b001), .eq(comparator_1_eq));  // open: gt, lt
  Comparator #(.width(3), .mode("unsigned")) comparator_2 (
    .a(demultiplexer_2_out1), .b(3'b001), .eq(comparator_2_eq));  // open: gt, lt
  Comparator #(.width(3), .mode("unsigned")) comparator_3 (
    .a(demultiplexer_1_out1), .b(demultiplexer_2_out1), .eq(comparator_3_eq));  // open: gt, lt
  xor xor_1 (xor_1_out, or_1_out, or_2_out);
  or or_3 (or_3_out, comparator_1_eq, comparator_2_eq);
  Comparator #(.width(6), .mode("unsigned")) comparator_4 (.a(adder_1_out), .b(6'b000101), .eq(V_K));  // open: gt, lt
  or or_4 (or_4_out, comparator_3_eq, xor_1_out);
  and and_1 (and_1_out, or_4_out, or_3_out);
  Multiplexer #(.select(2), .disabled(0)) multiplexer_3 (
    .in0(comparator_3_eq), .in1(or_4_out), .in2(and_1_out), .in3(xor_1_out), .out(V_BQKR), .sel(Select[1:0]),
    .en(Select[2]));

  // Notes on the sheet:
  //   0XX - Knight
  //   100 - Bishop
  //   101 - Queen
  //   110 - King
  //   111 - Rook
  //   Y signed bit
  //   X signed bit
  //   (dX)^2 +( dY)^2 = 5
  //   Set to 5(101)
  //   dx = dy
  //   Rook Validation
  //   Knight Validation
  //   Bishop Validation
  //   Queen Validation
  //   (magnitude only)
  //   (magnitude only)
  //   King Validation
endmodule

// Direction
module Direction_Encoding (
  input  [2:0] dX,
  input  X_sign,
  input  [2:0] dY,
  input  Y_sign,
  input  [2:0] Select,
  input  V_BQKR,
  input  V_K,
  input  Clk,
  output [2:0] D_BQKR,
  output No_Move,
  output [2:0] D_K
);

  wire comparator_1_eq, comparator_2_eq, d_ff_1_q, decoder_1_out1, decoder_1_out2, decoder_1_out3,
       decoder_1_out4, decoder_1_out5, decoder_1_out7, decoder_1_out10, decoder_1_out11, decoder_1_out15,
       demultiplexer_1_out0, demultiplexer_4_out0, multiplexer_4_out, not_1_out, or_2_out, or_3_out,
       or_4_out, xor_1_out;
  wire [1:0] counter_1_q;
  wire [2:0] demultiplexer_2_out0, demultiplexer_2_out1, demultiplexer_3_out0, demultiplexer_3_out1,
       multiplexer_1_out, multiplexer_2_out, or_1_out;
  wire [3:0] Y_out;

  Demultiplexer demultiplexer_1 (
    .out0(demultiplexer_1_out0), .out1(Y_out[3]), .in(X_sign), .sel(Select[2]));  // open: en
  Demultiplexer #(.width(3)) demultiplexer_2 (
    .out0(demultiplexer_2_out0), .out1(demultiplexer_2_out1), .in(dY), .sel(Select[2]));  // open: en
  Demultiplexer #(.width(3)) demultiplexer_3 (
    .out0(demultiplexer_3_out0), .out1(demultiplexer_3_out1), .in(dX), .sel(Select[2]));  // open: en
  or X (Y_out[1], demultiplexer_3_out1[0], demultiplexer_3_out1[1], demultiplexer_3_out1[2]);
  or Y (Y_out[0], demultiplexer_2_out1[0], demultiplexer_2_out1[1], demultiplexer_2_out1[2]);
  Demultiplexer demultiplexer_4 (
    .out0(demultiplexer_4_out0), .out1(Y_out[2]), .in(Y_sign), .sel(Select[2]));  // open: en
  Decoder #(.select(4)) decoder_1 (
    .out1(decoder_1_out1), .out2(decoder_1_out2), .out3(decoder_1_out3), .out4(decoder_1_out4),
    .out5(decoder_1_out5), .out6(decoder_1_out4), .out7(decoder_1_out7), .out8(decoder_1_out4),
    .out9(decoder_1_out4), .out10(decoder_1_out10), .out11(decoder_1_out11), .out12(decoder_1_out4),
    .out13(decoder_1_out4), .out14(decoder_1_out4), .out15(decoder_1_out15), .sel(Y_out), .en(V_BQKR));  // open: out0
  xor xor_1 (xor_1_out, V_BQKR, V_K);
  assign or_1_out = dX | dY;  // OR_Gate or_1, 3 bits wide
  Comparator #(.width(3)) comparator_1 (.a(demultiplexer_3_out0), .b(3'b010), .eq(comparator_1_eq));  // open: gt, lt
  Comparator #(.width(3)) comparator_2 (.a(demultiplexer_2_out0), .b(3'b010), .eq(comparator_2_eq));  // open: gt, lt
  Priority_Encoder priority_encoder_1 (
    .in0(decoder_1_out2), .in1(decoder_1_out3), .in2(decoder_1_out1), .in3(decoder_1_out11),
    .in4(decoder_1_out10), .in5(decoder_1_out15), .in6(decoder_1_out5), .in7(decoder_1_out7), .out(D_BQKR),
    .en_in(V_BQKR));  // open: gs, en_out
  or or_2 (or_2_out, or_1_out[0], or_1_out[1], or_1_out[2]);
  or or_3 (or_3_out, comparator_1_eq, comparator_2_eq);
  Counter #(.width(2), .max('h3), .ongoal("load")) counter_1 (
    .load(or_3_out), .D(2'b10), .count(d_ff_1_q), .Q(counter_1_q), .clk(Clk));  // open: carry, clr
  D_Flip_Flop d_ff_1 (.clk(Clk), .D(or_3_out), .Q(d_ff_1_q), .en(V_K));  // open: Qn, preset, reset
  nand nand_1 (No_Move, or_2_out, xor_1_out);
  Multiplexer #(.width(3)) multiplexer_1 (
    .in0(3'b000), .in1(3'b100), .out(multiplexer_1_out), .sel(demultiplexer_1_out0), .en(V_K));
  Multiplexer #(.width(3)) multiplexer_2 (
    .in0(3'b010), .in1(3'b110), .out(multiplexer_2_out), .sel(demultiplexer_4_out0), .en(V_K));
  or or_4 (or_4_out, counter_1_q[0], counter_1_q[1]);
  not not_1 (not_1_out, or_4_out);
  Multiplexer #(.width(3)) multiplexer_3 (
    .in0(multiplexer_1_out), .in1(multiplexer_2_out), .out(D_K), .sel(multiplexer_4_out), .en(V_K));
  Multiplexer multiplexer_4 (
    .in0(or_4_out), .in1(not_1_out), .out(multiplexer_4_out), .sel(comparator_1_eq));  // open: en
  // also tied to GND on the sheet: decoder_1_out4

  // Notes on the sheet:
  //   BQKR Direction (Uni-directional movement)
  //   No use
  //   Knight Direction
  //   dX = 2
  //   dY = 2
  //   +X/-X
  //   +Y/-Y
  //   Ask new inputs
endmodule

module Output (
  input  [2:0] dX,
  input  [2:0] dY,
  input  [2:0] Select,
  input  V_K,
  input  V_BQKR,
  input  [2:0] D_K,
  input  [2:0] D_BQKR,
  input  Clk,
  output Start_Stop_prime,
  output [2:0] Dir
);

  wire d_ff_1_q, multiplexer_1_out, or_1_out;
  wire [2:0] counter_1_q, multiplexer_2_out, multiplexer_3_out;

  Multiplexer multiplexer_1 (.in0(V_K), .in1(V_BQKR), .out(multiplexer_1_out), .sel(Select[2]));  // open: en
  or or_1 (or_1_out, D_BQKR[0], D_BQKR[1]);
  Multiplexer #(.width(3)) multiplexer_2 (
    .in0(3'b011), .in1(multiplexer_3_out), .out(multiplexer_2_out), .sel(Select[2]));  // open: en
  Multiplexer #(.width(3)) multiplexer_3 (.in0(dX), .in1(dY), .out(multiplexer_3_out), .sel(or_1_out), .en(V_BQKR));
  D_Flip_Flop d_ff_1 (.clk(Clk), .D(multiplexer_1_out), .Q(d_ff_1_q));  // open: Qn, preset, en, reset
  Counter #(.width(3), .max('h7), .ongoal("load")) counter_1 (
    .load(multiplexer_1_out), .D(multiplexer_2_out), .count(d_ff_1_q), .Q(counter_1_q), .clk(Clk));  // open: carry, clr
  or or_2 (Start_Stop_prime, counter_1_q[0], counter_1_q[1], counter_1_q[2]);
  Multiplexer #(.width(3)) multiplexer_4 (.in0(D_K), .in1(D_BQKR), .out(Dir), .sel(Select[2]));  // open: en
endmodule

// Edge
module Register_edge (
  input  clk,
  input  [2:0] D,
  input  en,
  input  reset,
  input  [2:0] val,
  output [2:0] Q
);

  wire demultiplexer_1_out0, demultiplexer_1_out1, demultiplexer_2_out0, demultiplexer_2_out1,
       demultiplexer_3_out0, demultiplexer_3_out1;

  Demultiplexer demultiplexer_1 (
    .out0(demultiplexer_1_out0), .out1(demultiplexer_1_out1), .in(reset), .sel(val[0]));  // open: en
  D_Flip_Flop #(.trigger("falling")) D0 (
    .clk(clk), .D(D[0]), .Q(Q[0]), .preset(demultiplexer_1_out1), .en(en), .reset(demultiplexer_1_out0));  // open: Qn
  Demultiplexer demultiplexer_2 (
    .out0(demultiplexer_2_out0), .out1(demultiplexer_2_out1), .in(reset), .sel(val[1]));  // open: en
  D_Flip_Flop #(.trigger("falling")) D1 (
    .clk(clk), .D(D[1]), .Q(Q[1]), .preset(demultiplexer_2_out1), .en(en), .reset(demultiplexer_2_out0));  // open: Qn
  Demultiplexer demultiplexer_3 (
    .out0(demultiplexer_3_out0), .out1(demultiplexer_3_out1), .in(reset), .sel(val[2]));  // open: en
  D_Flip_Flop #(.trigger("falling")) D2 (
    .clk(clk), .D(D[2]), .Q(Q[2]), .preset(demultiplexer_3_out1), .en(en), .reset(demultiplexer_3_out0));  // open: Qn

  // Notes on the sheet:
  //   Custom register that can be reset to a specific value asynchronously
endmodule

// Lvl
module Register_lvl (
  input  clk,
  input  [2:0] D,
  input  en,
  input  reset,
  input  [2:0] val,
  output [2:0] Q
);

  wire demultiplexer_1_out0, demultiplexer_1_out1, demultiplexer_2_out0, demultiplexer_2_out1,
       demultiplexer_3_out0, demultiplexer_3_out1;

  Demultiplexer demultiplexer_1 (
    .out0(demultiplexer_1_out0), .out1(demultiplexer_1_out1), .in(reset), .sel(val[0]));  // open: en
  D_Flip_Flop #(.trigger("high")) D0 (
    .clk(clk), .D(D[0]), .Q(Q[0]), .preset(demultiplexer_1_out1), .en(en), .reset(demultiplexer_1_out0));  // open: Qn
  Demultiplexer demultiplexer_2 (
    .out0(demultiplexer_2_out0), .out1(demultiplexer_2_out1), .in(reset), .sel(val[1]));  // open: en
  D_Flip_Flop #(.trigger("high")) D1 (
    .clk(clk), .D(D[1]), .Q(Q[1]), .preset(demultiplexer_2_out1), .en(en), .reset(demultiplexer_2_out0));  // open: Qn
  Demultiplexer demultiplexer_3 (
    .out0(demultiplexer_3_out0), .out1(demultiplexer_3_out1), .in(reset), .sel(val[2]));  // open: en
  D_Flip_Flop #(.trigger("high")) D2 (
    .clk(clk), .D(D[2]), .Q(Q[2]), .preset(demultiplexer_3_out1), .en(en), .reset(demultiplexer_3_out0));  // open: Qn

  // Notes on the sheet:
  //   Custom register that can be reset to a specific value asynchronously
endmodule

module Pawn_Valid (
  input  [2:0] Xout,
  input  [2:0] X0,
  input  [2:0] Yout,
  input  [2:0] Y0,
  input  [2:0] Xout_2,
  input  [2:0] X0_2,
  input  [2:0] Yout_2,
  input  [2:0] Y0_2,
  output [2:0] dX,
  output [2:0] dY,
  output [2:0] dX_2,
  output [2:0] dY_2
);

  wire and_1_out, and_2_out, and_3_out, comparator_1_eq, comparator_2_eq, comparator_3_eq, comparator_4_eq,
       comparator_5_eq, comparator_6_eq, or_1_out;

  Subtractor #(.width(3)) subtractor_1 (.a(Xout), .b(X0), .out(dX));  // open: bin, bout
  Subtractor #(.width(3)) subtractor_2 (.a(Yout), .b(Y0), .out(dY));  // open: bin, bout
  Subtractor #(.width(3)) subtractor_3 (.a(Xout_2), .b(X0_2), .out(dX_2));  // open: bin, bout
  Subtractor #(.width(3)) subtractor_4 (.a(Yout_2), .b(Y0_2), .out(dY_2));  // open: bin, bout
  Comparator #(.width(3), .mode("unsigned")) comparator_1 (.a(Y0_2), .b(3'b001), .eq(comparator_1_eq));  // open: gt, lt
  Comparator #(.width(3), .mode("unsigned")) comparator_2 (.a(3'b000), .b(dX), .eq(comparator_2_eq));  // open: gt, lt
  Comparator #(.width(3), .mode("unsigned")) comparator_3 (.a(dY), .b(3'b001), .eq(comparator_3_eq));  // open: gt, lt
  and and_1 (and_1_out, comparator_2_eq, comparator_3_eq);
  Comparator #(.width(3), .mode("unsigned")) comparator_4 (.a(3'b000), .b(dX_2), .eq(comparator_4_eq));  // open: gt, lt
  Comparator #(.width(3), .mode("unsigned")) comparator_5 (.a(3'b001), .b(dY_2), .eq(comparator_5_eq));  // open: gt, lt
  Comparator #(.width(3), .mode("unsigned")) comparator_6 (.a(dY_2), .b(3'b010), .eq(comparator_6_eq));  // open: gt, lt
  or or_1 (or_1_out, comparator_5_eq, and_2_out);
  and and_2 (and_2_out, comparator_6_eq, comparator_1_eq);
  and and_3 (and_3_out, comparator_4_eq, or_1_out);

  // Notes on the sheet:
  //   Pawn Validation (Aarabdh)
endmodule

module Obstacle (
  input  [5:0] in_1,
  input  [1:0] in_2,
  input  in_3,
  input  in_4,
  output [1:0] out_5
);

  RAM #(.addrWidth(6), .dataWidth(2), .bus("separate")) ram_1 (
    .addr(in_1), .din(in_2), .data(out_5), .clk(in_3), .ld(in_4));  // open: str, sel, clr

  // Notes on the sheet:
  //   Obstacle avoidance capability
  //   Using RAM
  //   Just explain
endmodule
